# Fritzing sketch I2S_FG_UI+Power_Supply+PCM5102A+LCD_DirectDrive (saved by Fritzing 0.9.2b)
breadboards: 3
perfboards: 5

parts:
  J1 = female pin header, 26 pins [form="♀ (female)"]  # not connected
  J2 = female pin header, 26 pins [form="♀ (female)"]  # not connected
  X1 = USB Connectors [package=usb-minib-nostop]  # not connected
  VCC1 = Battery
  J3 = female pin header, 8 pins [form="♀ (female)"]  # not connected
  XTAL1 = Crystal [frequency="16 Mhz" package=THT]
  U2 = Voltage Regulator - 5V [package="TO220 [THT]"]
  C3 = Ceramic Capacitor [capacitance=100nF package="100 mil [THT, multilayer]"]
  C4 = Ceramic Capacitor [capacitance=100nF package="100 mil [THT, multilayer]"]
  C5 = Electrolytic Capacitor [capacitance=1µF package="100 mil [THT, electrolytic]"]
  D1 = Rectifier Diode [part_number=1N4001 package="300 mil [THT]"]
  C6 = Electrolytic Capacitor [capacitance=1µF package="100 mil [THT, electrolytic]"]
  RE1 = Rotary Encoder [package=THT]
  C7 = Ceramic Capacitor [capacitance=100nF package="100 mil [THT, multilayer]"]
  C8 = Ceramic Capacitor [capacitance=100nF package="100 mil [THT, multilayer]"]
  J4 = female pin header, 7 pins [form="♀ (female)"]  # not connected
  J5 = female pin header, 7 pins [form="♀ (female)"]  # not connected
  U3 = mystery part, 5 pins [chip_label=AQM0802]
  C9 = Electrolytic Capacitor [capacitance=1µF package="100 mil [THT, electrolytic]"]
  C13 = Electrolytic Capacitor [capacitance=1µF package="100 mil [THT, electrolytic]"]
  U4 = mystery part, 20 pins [chip_label=PCM5102A]
  C14 = Ceramic Capacitor [capacitance=100nF package="100 mil [THT, multilayer]"]
  C15 = Ceramic Capacitor [capacitance=100nF package="100 mil [THT, multilayer]"]
  R3 = Resistor [tolerance=±5% resistance=470 package=THT]
  R4 = Resistor [tolerance=±5% resistance=470 package=THT]
  C16 = Ceramic Capacitor [capacitance=100nF package="100 mil [THT, multilayer]"]
  C17 = Ceramic Capacitor [capacitance=100nF package="100 mil [THT, multilayer]"]
  C18 = Ceramic Capacitor [capacitance=100nF package="100 mil [THT, multilayer]"]
  C19 = Ceramic Capacitor [capacitance=100nF package="100 mil [THT, multilayer]"]
  C20 = Electrolytic Capacitor [capacitance=1µF package="100 mil [THT, electrolytic]"]
  C21 = Electrolytic Capacitor [capacitance=1µF package="100 mil [THT, electrolytic]"]
  C22 = Ceramic Capacitor [capacitance=100nF package="100 mil [THT, multilayer]"]
  C23 = Ceramic Capacitor [capacitance=100nF package="100 mil [THT, multilayer]"]
  C24 = Electrolytic Capacitor [capacitance=1µF package="100 mil [THT, electrolytic]"]
  R5 = Resistor [tolerance=±5% resistance=100k package=THT]
  R6 = Resistor [tolerance=±5% resistance=100k package=THT]
  LED1 = LED - 5mm [color="Red (633nm)" package="5 mm [THT]"]
  R7 = Resistor [tolerance=±5% resistance=1k package=THT]

nets:
  N1: VCC1.-, U2.GND, C3.0, C4.1, C5.-, C6.-, RE1.EncoderPinC, C7.1, C8.1, U3.pin5, C9.-, R5.Pin_1, LED1.cathode
  N2: VCC1.+, U2.input_voltage, C3.1, C5.+, D1.cathode, R7.Pin_0
  N3: XTAL1.pin_0, C8.0
  N4: XTAL1.pin_1, C7.0
  N5: U2.output_voltage, C4.0, D1.anode, C6.+, R6.Pin_1
  N6: U3.pin1, C9.+
  N7: C13.-, U4.pin3, U4.pin9, U4.pin10, U4.pin11, U4.pin12, U4.pin16, U4.pin19, C14.1, C16.1, C17.0, C18.0, C19.1, C20.-, C21.-, C22.1, C23.1, C24.-
  N8: C13.+, U4.pin18, C22.0
  N9: U4.pin1, U4.pin8, U4.pin17, U4.pin20, C18.1, C19.0, C20.+, C21.+, C23.0, C24.+
  N10: U4.pin2, C15.0
  N11: U4.pin4, C15.1
  N12: U4.pin5, C14.0
  N13: U4.pin6, R4.Pin_1
  N14: U4.pin7, R3.Pin_1
  N15: R3.Pin_0, C17.1
  N16: R4.Pin_0, C16.0
  N17: R5.Pin_0, R6.Pin_0
  N18: LED1.anode, R7.Pin_1

notes:
  AQM0802
  1 VDD
  2 !RST
  3 SCL
  4 SDA
  5 GND
  +4.5V
  GND
  +3.3V
  GND
  KeyPad
  PSoC 5LP Prototyping Kit
  Kit Prog
  I2C Pull up
  in PSoC
  +3.3V
  GND(SW)
  AGND
  AVDD 3.3V
  DGND
  DVDD 3.3V
  OUTR
  OUTL
  PCM5102A
  1 CPVDD 20 DVDD
  2 CAPP 19 DGND
  3 CPGND 18 LDOO
  4 CAPM 17 XSMT
  5 VNEG 16 FMT
  6 OUTL 15 LRCK
  7 OUTR 14 DIN
  8 AVDD 13 BCK
  9 AGND 12 SCK
  10 DEMP 11 FLT
