# Fritzing sketch I2S_FG_UI+Power_Supply (saved by Fritzing 0.9.2b)
breadboards: 2
perfboards: 5

parts:
  J1 = female pin header, 26 pins [form="♀ (female)"]  # not connected
  J2 = female pin header, 26 pins [form="♀ (female)"]  # not connected
  X1 = USB Connectors [package=usb-minib-nostop]  # not connected
  VCC1 = Battery
  J3 = female pin header, 8 pins [form="♀ (female)"]  # not connected
  XTAL1 = Crystal [frequency="16 Mhz" package=THT]
  U2 = Voltage Regulator - 5V [package="TO220 [THT]"]
  C3 = Ceramic Capacitor [capacitance=100nF package="100 mil [THT, multilayer]"]
  C4 = Ceramic Capacitor [capacitance=100nF package="100 mil [THT, multilayer]"]
  C5 = Electrolytic Capacitor [capacitance=1µF package="100 mil [THT, electrolytic]"]
  D1 = Rectifier Diode [part_number=1N4001 package="300 mil [THT]"]
  C6 = Electrolytic Capacitor [capacitance=1µF package="100 mil [THT, electrolytic]"]
  RE1 = Rotary Encoder [package=THT]
  C7 = Ceramic Capacitor [capacitance=100nF package="100 mil [THT, multilayer]"]
  C8 = Ceramic Capacitor [capacitance=100nF package="100 mil [THT, multilayer]"]
  J4 = female pin header, 7 pins [form="♀ (female)"]  # not connected
  J5 = female pin header, 7 pins [form="♀ (female)"]  # not connected
  U3 = mystery part, 5 pins [chip_label=AQM0802]
  Q2 = Basic FET N-Channel [package="TO220 [THT]"]
  C9 = Electrolytic Capacitor [capacitance=1µF package="100 mil [THT, electrolytic]"]

nets:
  N1: VCC1.-, U2.GND, C3.0, C4.1, C5.-, C6.-, RE1.EncoderPinC, C7.1, C8.1, Q2.gate
  N2: VCC1.+, U2.input_voltage, C3.1, C5.+, D1.cathode
  N3: XTAL1.pin_0, C8.0
  N4: XTAL1.pin_1, C7.0
  N5: U2.output_voltage, C4.0, D1.anode, C6.+, U3.pin1, C9.+
  N6: U3.pin5, Q2.source, C9.-

notes:
  AQM0802
  1 VDD
  2 !RST
  3 SCL
  4 SDA
  5 GND
  +4.5V
  GND
  +3.3V
  GND
  KeyPad
  PSoC 5LP Prototyping Kit
  Kit Prog
  2N7000
  S G D
  I2C Pull up
  in PSoC
  +3.3V
  GND(SW)
