# Fritzing sketch I2S_FG_UI (saved by Fritzing 0.9.2b)
breadboards: 3
perfboards: 4

parts:
  J1 = female pin header, 26 pins [form="♀ (female)"]  # not connected
  J2 = female pin header, 26 pins [form="♀ (female)"]  # not connected
  X1 = USB Connectors [package=usb-minib-nostop]  # not connected
  J3 = female pin header, 8 pins [form="♀ (female)"]  # not connected
  U1 = mystery part, 5 pins [chip_label=AQM0802]
  XTAL1 = Crystal [frequency="16 Mhz" package=THT]
  RE1 = Rotary Encoder [package=THT]
  C7 = Ceramic Capacitor [capacitance=100nF package="100 mil [THT, multilayer]"]
  C8 = Ceramic Capacitor [capacitance=100nF package="100 mil [THT, multilayer]"]
  J4 = female pin header, 7 pins [form="♀ (female)"]  # not connected
  J5 = female pin header, 7 pins [form="♀ (female)"]  # not connected

nets:
  N1: U1.pin5, RE1.EncoderPinC, C7.1, C8.1
  N2: XTAL1.pin_0, C8.0
  N3: XTAL1.pin_1, C7.0

notes:
  AQM0802
  1 VDD
  2 !RST
  3 SCL
  4 SDA
  5 GND
  +3.3V
  GND
  KeyPad
  PSoC 5LP Prototyping Kit
  Kit Prog
  Pull up in PSoC
