# Fritzing sketch PCM5102A-PSoC 5LP CQ PMB (saved by Fritzing 0.9.2b)
breadboards: 1
perfboards: 1

parts:
  U1 = mystery part, 20 pins [chip_label=PCM5102A]
  C1 = Ceramic Capacitor [capacitance=100nF package="100 mil [THT, multilayer]"]
  C2 = Ceramic Capacitor [capacitance=100nF package="100 mil [THT, multilayer]"]
  R1 = Resistor [tolerance=±5% resistance=470 package=THT]
  R2 = Resistor [tolerance=±5% resistance=470 package=THT]
  C3 = Ceramic Capacitor [capacitance=100nF package="100 mil [THT, multilayer]"]
  C4 = Ceramic Capacitor [capacitance=100nF package="100 mil [THT, multilayer]"]
  C5 = Ceramic Capacitor [capacitance=100nF package="100 mil [THT, multilayer]"]
  C6 = Ceramic Capacitor [capacitance=100nF package="100 mil [THT, multilayer]"]
  C7 = Ceramic Capacitor [capacitance=100nF package="100 mil [THT, multilayer]"]
  C8 = Electrolytic Capacitor [capacitance=1µF package="100 mil [THT, electrolytic]"]
  C9 = Electrolytic Capacitor [capacitance=1µF package="100 mil [THT, electrolytic]"]
  X1 = USB Connectors [package=usb-minib]  # not connected
  X2 = USB Connectors [package=usb-minib]  # not connected
  J1 = female pin header, 20 pins [form="♀ (female)"]  # not connected
  J2 = female pin header, 20 pins [form="♀ (female)"]  # not connected
  J3 = female pin header, 20 pins [form="♀ (female)"]
  J4 = female pin header, 20 pins [form="♀ (female)"]

nets:
  N1: U1.pin1, U1.pin8, C5.1, C9.+, J4.pin3
  N2: U1.pin2, C1.0
  N3: U1.pin3, U1.pin9, C2.1, C3.0, C4.1, C5.0, C9.-, J3.pin3
  N4: U1.pin4, C1.1
  N5: U1.pin5, C2.0
  N6: U1.pin6, R2.Pin_1
  N7: U1.pin7, R1.Pin_1
  N8: U1.pin10, U1.pin11, U1.pin12, U1.pin16, U1.pin19, C6.1, C7.1, C8.-, J3.pin2
  N9: U1.pin13, J3.pin19
  N10: U1.pin14, J4.pin18
  N11: U1.pin15, J3.pin18
  N12: U1.pin17, U1.pin18, U1.pin20, C6.0, C7.0, C8.+, J4.pin2
  N13: R1.Pin_0, C3.1
  N14: R2.Pin_0, C4.0

notes:
  DGND
  DVDD 3.3V
  AGND
  AVDD 3.3V
  OUTR
  OUTL
  PCM5102A
  1 CPVDD 20 DVDD
  2 CAPP 19 DGND
  3 CPGND 18 LDOO
  4 CAPM 17 XSMT
  5 VNEG 16 FMT
  6 OUTL 15 LRCK
  7 OUTR 14 DIN
  8 AVDD 13 BCK
  9 AGND 12 SCK
  10 DEMP 11 FLT
  PSoC 5LP CQ PMB
  配線要チェック!
