# Fritzing sketch PCM5102a_FG_ケース内配線 (saved by Fritzing 0.9.2b)
perfboards: 2

parts:
  J1 = female pin header, 3 pins [form="♀ (female)"]
  J2 = female pin header, 3 pins [form="♀ (female)"]
  J3 = female pin header, 2 pins [form="♀ (female)"]
  J4 = female pin header, 8 pins [form="♀ (female)"]
  J5 = female pin header, 5 pins [form="♀ (female)"]  # not connected
  RE1 = Rotary Encoder [package=THT]
  J6 = female pin header, 8 pins [form="♀ (female)"]
  S1 = Toggle Switch [package=THT]
  VCC1 = 4 x AAA Battery Mount
  TRS1 = Audio Jack (TRS) 3.5mm [package="4Ucon 08780 [THT]"]

nets:
  N1: J1.pin1, RE1.EncoderPinC
  N2: J1.pin2, RE1.EncoderPinB
  N3: J1.pin3, RE1.EncoderPinA
  N4: J2.pin1, TRS1.Sleeve
  N5: J2.pin2, TRS1.Tip
  N6: J2.pin3, TRS1.Ring
  N7: J3.pin1, S1.COM
  N8: J3.pin2, VCC1.-
  N9: J4.pin1, J6.pin1
  N10: J4.pin2, J6.pin2
  N11: J4.pin3, J6.pin3
  N12: J4.pin4, J6.pin4
  N13: J4.pin5, J6.pin5
  N14: J4.pin6, J6.pin6
  N15: J4.pin7, J6.pin7
  N16: J4.pin8, J6.pin8

notes:
  RotaryEncoder
  G/B/A
  AQM0802
  V+/RST/SCL/SDA/GND
  KeyPad
  PWR
  V+/GND
  WAVEOUT
  GND
  Filterd
  Naked
  4.5V
